# Fritzing sketch stepper (saved by Fritzing 0.9.3b)
breadboards: 1

parts:
  Part1 = Arduino Nano (Rev3.0)
  Pololu_A1 = Pololu A4988 [package=SO16]

nets:
  N1: Part1.D2, Pololu_A1.DIR
  N2: Part1.D3, Pololu_A1.STEP
  N3: Part1.D4, Pololu_A1.ENABLE
  N4: Pololu_A1.RESET, Pololu_A1.SLEEP
